# Fritzing sketch led controller (saved by Fritzing 0.9.3b)
breadboards: 1

parts:
  Part1 = Arduino Uno (Rev3)
  S4 = Pushbutton [package="[SMD]"]
  LED1 = LED - 5mm [color="Red (633nm)" package="5 mm [THT]"]
  R2 = Resistor [tolerance=±5% resistance=220 package=THT]
  R1 = Resistor [tolerance=±5% resistance=10k package=THT]
  R5 = Resistor [tolerance=±5% resistance=10k package=THT]
  R4 = Photocell (LDR) [package=THT]
  R3 = Rotary Potentiometer (Small) [maximum_resistance=100kΩ package=THT]

nets:
  N1: Part1.A3, R5.Pin_0, R4.pin_1
  N2: Part1.A5/SCL, R3.wiper
  N3: Part1.D2, S4.Pin_1, S4.Pin_2, R1.Pin_0
  N4: Part1.D6_PWM, LED1.anode
  N5: Part1.5V, S4.Pin_3, S4.Pin_4, R4.pin_0, R3.leg1
  N6: Part1.GND, R2.Pin_1, R1.Pin_1, R5.Pin_1, R3.leg2
  N7: LED1.cathode, R2.Pin_0
