# Fritzing sketch color_controller (saved by Fritzing 0.9.3b)
breadboards: 1

parts:
  Part1 = Arduino Uno (Rev3)
  LED2 = RGB LED (com. cathode, rgb) [package="5 mm [THT]"]
  R6 = Resistor [tolerance=±5% resistance=220 package=THT]
  R7 = Resistor [tolerance=±5% resistance=220 package=THT]
  R2 = Resistor [tolerance=±5% resistance=220 package=THT]
  S1 = Pushbutton [package="[THT]"]
  S2 = Pushbutton [package="[THT]"]
  S3 = Pushbutton [package="[THT]"]
  R11 = Resistor [tolerance=±5% resistance=10k package=THT]
  R12 = Resistor [tolerance=±5% resistance=10k package=THT]
  R13 = Resistor [tolerance=±5% resistance=10k package=THT]
  R14 = PHOTOCELL [package=photocell-kit]
  R15 = Resistor [tolerance=±5% resistance=10k package=THT]

nets:
  N1: Part1.A1, R14.P$2, R15.Pin_0
  N2: Part1.D9_PWM, R2.Pin_1
  N3: Part1.D10_PWM/SS, R6.Pin_1
  N4: Part1.D11_PWM/MOSI, R7.Pin_1
  N5: Part1.5V, S1.Pin_3, S1.Pin_4, S2.Pin_3, S2.Pin_4, S3.Pin_3, S3.Pin_4, R14.P$1
  N6: Part1.GND, LED2.common_cathode, R11.Pin_1, R12.Pin_1, R13.Pin_1, R15.Pin_1
  N7: LED2.red_anode, R2.Pin_0
  N8: LED2.green_anode, R6.Pin_0
  N9: LED2.blue_anode, R7.Pin_0
  N10: S1.Pin_1, S1.Pin_2, R11.Pin_0
  N11: S2.Pin_1, S2.Pin_2, R12.Pin_0
  N12: S3.Pin_1, S3.Pin_2, R13.Pin_0

notes:
  220 - 330 ohm resistors on LED
  10K pulldown resistors on all sensors
