# Fritzing sketch resistors (saved by Fritzing 0.9.3b)
breadboards: 1

parts:
  Part1 = Arduino Uno (Rev3)
  R10 = Resistor [tolerance=±5% resistance=10k package=THT]
  R9 = Resistor [tolerance=±5% resistance=10k package=THT]
  R16 = Resistor [tolerance=±5% resistance=220 package=THT]
  R17 = Resistor [tolerance=±5% resistance=220 package=THT]

nets:
  N1: Part1.A0, R16.Pin_1
  N2: Part1.A1, R17.Pin_1
  N3: Part1.A2, Part1.5V, R9.Pin_0, R16.Pin_0
  N4: Part1.A3, Part1.GND, R10.Pin_0, R17.Pin_0
  N5: Part1.A4/SDA, R9.Pin_1
  N6: Part1.A5/SCL, R10.Pin_1

notes:
  10K resistors
  220 or 330 ohm resistors
