# Fritzing sketch keyboard (saved by Fritzing 0.9.3b)
breadboards: 1

parts:
  Part1 = Arduino Uno (Rev3)
  LED2 = RGB LED (com. cathode, rgb) [package="5 mm [THT]"]
  POT1 = Breadboard Trimpot
  R7 = Resistor [tolerance=±5% resistance=220 package=THT]
  R6 = Resistor [tolerance=±5% resistance=220 package=THT]
  R2 = Resistor [tolerance=±5% resistance=220 package=THT]
  S4 = Momentary Switch [package=ksa_sealed_tac_switch]
  S3 = Momentary Switch [package=ksa_sealed_tac_switch]
  S2 = Momentary Switch [package=ksa_sealed_tac_switch]
  S1 = Momentary Switch [package=ksa_sealed_tac_switch]
  R10 = Resistor [tolerance=±5% resistance=10k package=THT]
  R11 = Resistor [tolerance=±5% resistance=10k package=THT]
  R12 = Resistor [tolerance=±5% resistance=10k package=THT]
  R13 = Resistor [tolerance=±5% resistance=10k package=THT]
  J1 = Piezo Speaker

nets:
  N1: Part1.A0, POT1.PIN2
  N2: Part1.D9_PWM, R2.Pin_1
  N3: Part1.D10_PWM/SS, R6.Pin_1
  N4: Part1.D11_PWM/MOSI, R7.Pin_1
  N5: Part1.GND, LED2.common_cathode, POT1.PIN3, R10.Pin_1, R11.Pin_1, R12.Pin_1, R13.Pin_1, J1.pin1
  N6: Part1.D2, S1.2, R10.Pin_0
  N7: Part1.D3_PWM, S2.2, R11.Pin_0
  N8: Part1.D4, S3.2, R12.Pin_0
  N9: Part1.D5_PWM, S4.2, R13.Pin_0
  N10: Part1.D6_PWM, J1.pin2
  N11: Part1.5V, POT1.PIN1, S4.4, S3.4, S2.4, S1.4
  N12: LED2.red_anode, R2.Pin_0
  N13: LED2.green_anode, R6.Pin_0
  N14: LED2.blue_anode, R7.Pin_0

notes:
  10k Ohm Resistors on Buttons
  220 Ohm Resistors on RGB LED
