# Fritzing sketch weatherstation 2 (saved by Fritzing 0.9.3b)
breadboards: 1

parts:
  Part1 = Arduino Uno (Rev3)
  LED2 = RGB LED (com. cathode, rgb) [package="5 mm [THT]"]
  DHT1 = DHT11 Humitidy and Temperature Sensor
  hc-sr1 = hc-sr04
  R8 = PHOTOCELL [package=photocell]
  POT1 = Breadboard Trimpot
  M1 = DC Motor
  R7 = Resistor [tolerance=±5% resistance=220 package=THT]
  R6 = Resistor [tolerance=±5% resistance=220 package=THT]
  R2 = Resistor [tolerance=±5% resistance=220 package=THT]
  R10 = Resistor [tolerance=±5% resistance=10k package=THT]

nets:
  N1: Part1.A3, M1.pin_2
  N2: Part1.A4/SDA, POT1.PIN2
  N3: Part1.A5/SCL, R8.P$2, R10.Pin_0
  N4: Part1.D8, hc-sr1.Trig
  N5: Part1.D9_PWM, R2.Pin_1
  N6: Part1.D10_PWM/SS, R6.Pin_1
  N7: Part1.D11_PWM/MOSI, R7.Pin_1
  N8: Part1.D2, DHT1.DATA
  N9: Part1.D7, hc-sr1.Echo
  5V: Part1.5V, DHT1.VDD, hc-sr1.VCC, R8.P$1, POT1.PIN1
  GND: Part1.GND, LED2.common_cathode, DHT1.GND, hc-sr1.GND, POT1.PIN3, M1.pin_1, R10.Pin_1
  N10: LED2.red_anode, R2.Pin_0
  N11: LED2.green_anode, R6.Pin_0
  N12: LED2.blue_anode, R7.Pin_0

notes:
  220 Ohm Resistors on RGB LED
  DHT11 breakout rearranges the internal pins as shown in the wire colors below.
  10K Ohm Resistor on Photoresistor

custom parts:
  DHT11 Humitidy and Temperature Sensor: DHT11 Humidity and Temperature Sensor
