# Fritzing sketch motors (saved by Fritzing 0.9.3b)
breadboards: 1

parts:
  Part1 = Arduino Uno (Rev3)
  LED2 = RGB LED (com. cathode, rgb) [package="5 mm [THT]"]
  Q1 = NPN-Transistor [package="TO92 [THT]"]
  M1 = DC Motor
  J1 = Basic Servo
  D1 = Rectifier Diode [part_number=1N4001 package="300 mil [THT]"]
  R8 = Resistor [tolerance=±5% resistance=220 package=THT]
  R2 = Resistor [tolerance=±5% resistance=220 package=THT]
  R7 = Resistor [tolerance=±5% resistance=220 package=THT]
  R6 = Resistor [tolerance=±5% resistance=220 package=THT]
  VCC1 = Battery

nets:
  N1: Part1.D9_PWM, R2.Pin_1
  N2: Part1.D10_PWM/SS, R6.Pin_1
  N3: Part1.D11_PWM/MOSI, R7.Pin_1
  N4: Part1.D3_PWM, R8.Pin_0
  N5: Part1.D5_PWM, J1.pulse
  5V: Part1.5V, J1.vcc
  GND: Part1.GND, LED2.common_cathode, J1.gnd
  N6: LED2.red_anode, R2.Pin_0
  N7: LED2.green_anode, R6.Pin_0
  N8: LED2.blue_anode, R7.Pin_0
  N9: Q1.E, VCC1.-
  N10: Q1.B, R8.Pin_1
  N11: Q1.C, M1.pin_1, D1.anode
  N12: M1.pin_2, D1.cathode, VCC1.+

notes:
  220 Ohm Resistor for Transistor
